# Fritzing sketch joystick (saved by Fritzing 0.9.3b)
circuit board: 5.16903cm x 7.00112cm

parts:
  Alimentation = female pin header, 2 pins [form="♀ (female)"]
  R1 = Resistor [tolerance=±5% resistance=1k package=THT]
  IC2 = 74LS38 [chip_label=IC package="DIP (Dual Inline) [THT]"]
  IC2_PWR = 74LS38 [package="DIP (Dual Inline) [THT]"]
  IC2_4 = 74LS38 [package="DIP (Dual Inline) [THT]"]
  IC2_3 = 74LS38 [package="DIP (Dual Inline) [THT]"]
  IC2_2 = 74LS38 [package="DIP (Dual Inline) [THT]"]
  IC2_1 = 74LS38 [package="DIP (Dual Inline) [THT]"]
  Amstrad = female pin header, 7 pins [form="♀ (female)"]
  ESP_b = rounded female pin header, 19 pins [form="♀ (female rounded)"]
  ESP_t = rounded female pin header, 19 pins [form="♀ (female rounded)"]
  IC1_1 = 74LS38 [package="DIP (Dual Inline) [THT]"]
  IC1_3 = 74LS38 [package="DIP (Dual Inline) [THT]"]
  IC1 = 74LS38 [chip_label=IC package="DIP (Dual Inline) [THT]"]
  IC1_PWR = 74LS38 [package="DIP (Dual Inline) [THT]"]
  IC1_4 = 74LS38 [package="DIP (Dual Inline) [THT]"]
  IC1_2 = 74LS38 [package="DIP (Dual Inline) [THT]"]

nets:
  5V: Alimentation.pin1, R1.Pin_0, IC2.connector13, IC2_PWR.pin14, ESP_b.pin19, IC1.connector13, IC1_PWR.pin14
  GND: Alimentation.pin2, IC2.connector3, IC2.connector4, IC2.connector5, IC2.connector6, IC2_PWR.pin7, IC2_2.pin4, IC2_2.pin5, IC2_2.pin6, ESP_t.pin1, IC1.connector6, IC1_PWR.pin7
  N1: R1.Pin_1, IC2.connector0, IC2.connector8, IC2.connector11, IC2_4.pin12, IC2_3.pin9, IC2_1.pin1, IC1_1.pin1, IC1_3.pin9, IC1.connector0, IC1.connector5, IC1.connector8, IC1.connector11, IC1_4.pin12, IC1_2.pin6
  UC_Down: IC2.connector1, IC2_1.pin2, ESP_b.pin11
  Down: IC2.connector2, IC2_1.pin3, Amstrad.pin5
  Left: IC2.connector7, IC2_3.pin8, Amstrad.pin7
  UC_Left: IC2.connector9, IC2_3.pin10, ESP_b.pin12
  Right: IC2.connector10, IC2_4.pin11, Amstrad.pin6
  UC_Right: IC2.connector12, IC2_4.pin13, ESP_b.pin13
  Fire1: Amstrad.pin1, IC1_1.pin3, IC1.connector2
  Common: Amstrad.pin2, IC1.connector3, IC1.connector4, IC1_2.pin4, IC1_2.pin5
  Fire2: Amstrad.pin3, IC1_3.pin8, IC1.connector7
  Up: Amstrad.pin4, IC1.connector10, IC1_4.pin11
  UC_Fire1: ESP_b.pin8, IC1_1.pin2, IC1.connector1
  UC_Up: ESP_b.pin9, IC1.connector12, IC1_4.pin13
  UC_Fire2: ESP_b.pin10, IC1_3.pin10, IC1.connector9

custom parts:
  74LS38: 74LS38 AND Gate
  74LS38: 74LS38 AND Gate
  74LS38: 74LS38 AND Gate
  74LS38: 74LS38 AND Gate
  74LS38: 74LS38 AND Gate
  74LS38: 74LS38 AND Gate
